# Fritzing sketch CircuitDiagram (saved by Fritzing 0.9.6b)
breadboards: 2

parts:
  S5 = Pushbutton [package="[THT]"]
  S6 = Pushbutton [package="[THT]"]
  S7 = Pushbutton [package="[THT]"]
  S8 = Pushbutton [package="[THT]"]
  LED6 = LED - 5mm [color="Red (633nm)" current=0.030 package="5 mm [THT]"]
  LED7 = LED - 5mm [color="Red (633nm)" current=0.030 package="5 mm [THT]"]
  LED8 = LED - 5mm [color="Red (633nm)" current=0.030 package="5 mm [THT]"]
  R5 = Resistor [tolerance=±5% resistance=220 package="1206 [SMD]"]
  R6 = Resistor [tolerance=±5% resistance=220 package="1206 [SMD]"]
  R7 = Resistor [tolerance=±5% resistance=220 package="1206 [SMD]"]
  R8 = Resistor [tolerance=±5% resistance=220 package="1206 [SMD]"]
  S9 = Pushbutton [package="[THT]"]
  HC-SR04_Sensor_1 = HC-SR04 Ultrasonic Distance Sensor
  LED5 = LED - 5mm [color="Red (633nm)" current=0.030 package="5 mm [THT]"]
  R9 = Resistor [tolerance=±5% power=0.25 resistance=220 package=THT]
  R10 = Resistor [tolerance=±5% power=0.25 resistance=220 package=THT]

nets:
  N1: S5.Pin_1, S5.Pin_2, S6.Pin_1, S6.Pin_2, S7.Pin_1, S7.Pin_2, S8.Pin_1, S8.Pin_2
  N2: S5.Pin_3, S5.Pin_4
  N3: S6.Pin_3, S6.Pin_4
  N4: S7.Pin_3, S7.Pin_4
  N5: S8.Pin_3, S8.Pin_4
  GND: LED6.cathode, LED8.cathode, LED5.cathode
  N6: LED6.anode, R6.Pin_1
  N7: LED7.anode, R7.Pin_0, R7.Pin_1
  N8: LED8.anode, R8.Pin_1
  N9: R5.Pin_0, R6.Pin_0, R8.Pin_0
  N10: R5.Pin_1, LED5.anode
  N11: S9.Pin_1, S9.Pin_2
  N12: S9.Pin_3, S9.Pin_4
  N13: HC-SR04_Sensor_1.VCC, R10.Pin_1
  N14: HC-SR04_Sensor_1.TRIG, R9.Pin_1
  N15: R9.Pin_0, R10.Pin_0

notes:
  Zach - Lights n stuff
  Blue, Green, pins 12, 13, 16, 19-21
  Ethan - The Button, pin 22
  Red
  Matthew, Wires
  23, 24, 25, 26, 27
  White
  Matthew
  Sonic Sensor
  Yellow, pins 4, 5
